# Fritzing sketch Sketch (saved by Fritzing 0.9.3b)
breadboards: 1

parts:
  M1 = DC Motor  # not connected
  M2 = DC Motor  # not connected
  L298N1 = L298N DC motor driver
  Raspberry_Pi_1 = Raspberry Pi 3 [part_number=RPI-3-V1.2]
  BAT1 = 18650 battery holder [package=battery-18650-kit]
  hc-sr1 = hc-sr04

nets:
  N1: L298N1.12V, BAT1.+
  GND: L298N1.GND, Raspberry_Pi_1.GND, BAT1.-, hc-sr1.GND
  N2: L298N1.ENA, Raspberry_Pi_1.GIPO18
  N3: L298N1.ENB, Raspberry_Pi_1.GIPO24
  N4: L298N1.IN1, Raspberry_Pi_1.GIPO17
  N5: L298N1.IN2, Raspberry_Pi_1.GIPO27
  N6: L298N1.IN3, Raspberry_Pi_1.GIPO22
  N7: L298N1.IN4, Raspberry_Pi_1.GIPO23
  N8: Raspberry_Pi_1.GPIO2, hc-sr1.Trig
  N9: Raspberry_Pi_1.GPIO3, hc-sr1.Echo
  5V: Raspberry_Pi_1.5V, hc-sr1.VCC

custom parts:
  L298N DC motor driver: 2x DC motor driver with 78M05 positive voltage regulator (7..35 V) L298N: max 46 V, 2 A Set 5 V Enable jumper to enable 5 V regultor (needed for the L298N) and +5 V output at screw terminal or supply external +5 V at screw terminal Set ENA and/or ENB to +5 V to enable motor permanently or supply ENA and/or ENB with PWM signal IN1 and IN2 set rotation directory for motor A (OUT1/OUT2) IN2 and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
  18650 battery holder: 18650 Battery Holder
